# Fritzing sketch schemalicenta (saved by Fritzing 0.9.3b)
breadboards: 5

parts:
  YwRobot_Power_Supply1 = YwRobot Breadboard Power Supply [part_number=545043]
  Teensy1 = Teensy 3.6 (Basic)
  hc-sr1 = hc-sr04
  hc-sr2 = hc-sr04
  hc-sr3 = hc-sr04
  LED2 = smd LED [color="Red (633nm)" package="0805 [SMD]"]
  LED3 = smd LED [color="Red (633nm)" package="0805 [SMD]"]
  R2 = Resistor [tolerance=±5% resistance=150 package="0603 [SMD]"]
  R3 = Resistor [tolerance=±5% resistance=150 package="0603 [SMD]"]
  S1 = Reed switch [package=THT]
  S2 = Reed switch [package=THT]
  S3 = Reed switch [package=THT]
  KY-1 = Keyes Relay [package=THT]
  KY-2 = Keyes Relay [package=THT]
  KY-3 = Keyes Relay [package=THT]
  LED4 = smd LED [color="Red (633nm)" package="0805 [SMD]"]
  R4 = Resistor [tolerance=±5% resistance=150 package="0603 [SMD]"]
  LED5 = smd LED [color="Red (633nm)" package="0805 [SMD]"]
  R5 = Resistor [tolerance=±5% resistance=150 package="0603 [SMD]"]
  Q1 = Basic FET N-Channel [package="TO220 [THT]"]
  Q2 = Basic FET N-Channel [package="TO220 [THT]"]
  Q3 = Basic FET N-Channel [package="TO220 [THT]"]
  R6 = Resistor [tolerance=±5% resistance=10k package="0603 [SMD]"]
  R7 = Resistor [tolerance=±5% resistance=10k package="0603 [SMD]"]
  R8 = Resistor [tolerance=±5% resistance=10k package="0603 [SMD]"]
  LED6 = RGB LED (com. cathode, rgb) [package="5 mm [THT]"]
  U1 = RFID RC522 SIP - 8 pins [chip_label="RFID RC522" package="SIP (Single Inline) [THT]"]
  Keypad4x1 = Keypad Membran 4x4
  U2 = LCD-16X2 [package=lcd-16x2]  # not connected
  ML1 = MagLock
  ML2 = MagLock
  LED7 = LEDs [package=led10mm]
  Part1 = SMD5050 s  # not connected
  Part2 = SMD5050 s  # not connected
  Part3 = SMD5050 s  # not connected
  KY-4 = Keyes Relay [package=THT]
  ML3 = MagLock
  S4 = Round Pushbutton
  S5 = Round Pushbutton
  S6 = Round Pushbutton
  S7 = Round Pushbutton
  S8 = Round Pushbutton
  R10 = Photocell (LDR) [package=THT]
  R11 = Resistor [tolerance=±5% resistance=220 package="2512 [SMD]"]
  R12 = Resistor [tolerance=±5% resistance=220 package="2512 [SMD]"]
  R13 = Resistor [tolerance=±5% resistance=220 package="2512 [SMD]"]
  R14 = Photocell (LDR) [package=THT]
  R15 = Photocell (LDR) [package=THT]
  LED9 = smd LED [color="Yellow (595nm)" package="0805 [SMD]"]
  R16 = Resistor [tolerance=±5% resistance=150 package="0603 [SMD]"]
  LED10 = smd LED [color="Red (633nm)" package="0805 [SMD]"]  # not connected
  LED11 = smd LED [color="Red (633nm)" package="0805 [SMD]"]
  R18 = Resistor [tolerance=±5% resistance=150 package="0603 [SMD]"]
  LED12 = smd LED [color="Red (633nm)" package="0805 [SMD]"]  # not connected
  LED13 = smd LED [color="Red (633nm)" package="0805 [SMD]"]  # not connected
  LED14 = smd LED [color="Red (633nm)" package="0805 [SMD]"]
  R19 = Resistor [tolerance=±5% resistance=150 package="0603 [SMD]"]
  LED15 = smd LED [color="Red (633nm)" package="0805 [SMD]"]  # not connected
  LED16 = smd LED [color="Red (633nm)" package="0805 [SMD]"]  # not connected
  LED17 = smd LED [color="Red (633nm)" package="0805 [SMD]"]  # not connected
  LED18 = smd LED [color="Red (633nm)" package="0805 [SMD]"]
  R20 = Resistor [tolerance=±5% resistance=150 package="0603 [SMD]"]
  LED19 = smd LED [color="Red (633nm)" package="0805 [SMD]"]  # not connected
  LED20 = smd LED [color="Red (633nm)" package="0805 [SMD]"]  # not connected
  LED21 = smd LED [color="Red (633nm)" package="0805 [SMD]"]  # not connected
  LED22 = smd LED [color="Red (633nm)" package="0805 [SMD]"]
  R21 = Resistor [tolerance=±5% resistance=150 package="0603 [SMD]"]
  LED23 = smd LED [color="Red (633nm)" package="0805 [SMD]"]  # not connected
  LED24 = smd LED [color="Red (633nm)" package="0805 [SMD]"]  # not connected
  LED25 = smd LED [color="Red (633nm)" package="0805 [SMD]"]  # not connected
  LED26 = smd LED [color="Red (633nm)" package="0805 [SMD]"]
  R22 = Resistor [tolerance=±5% resistance=150 package="0603 [SMD]"]
  LED27 = smd LED [color="Red (633nm)" package="0805 [SMD]"]  # not connected
  LED28 = smd LED [color="Red (633nm)" package="0805 [SMD]"]  # not connected
  LED29 = smd LED [color="Red (633nm)" package="0805 [SMD]"]  # not connected
  LED30 = smd LED [color="Red (633nm)" package="0805 [SMD]"]
  R23 = Resistor [tolerance=±5% resistance=150 package="0603 [SMD]"]
  LED31 = smd LED [color="Red (633nm)" package="0805 [SMD]"]  # not connected
  LED32 = smd LED [color="Red (633nm)" package="0805 [SMD]"]  # not connected
  LED33 = smd LED [color="Red (633nm)" package="0805 [SMD]"]  # not connected
  LED34 = smd LED [color="Red (633nm)" package="0805 [SMD]"]
  R24 = Resistor [tolerance=±5% resistance=150 package="0603 [SMD]"]
  LED35 = smd LED [color="Red (633nm)" package="0805 [SMD]"]  # not connected
  LED36 = smd LED [color="Red (633nm)" package="0805 [SMD]"]  # not connected
  LED37 = smd LED [color="Red (633nm)" package="0805 [SMD]"]  # not connected
  LED38 = smd LED [color="Red (633nm)" package="0805 [SMD]"]
  R25 = Resistor [tolerance=±5% resistance=150 package="0603 [SMD]"]
  LED39 = smd LED [color="Red (633nm)" package="0805 [SMD]"]  # not connected
  LED40 = smd LED [color="Red (633nm)" package="0805 [SMD]"]  # not connected
  LED41 = smd LED [color="Red (633nm)" package="0805 [SMD]"]  # not connected
  S9 = Reed switch [package=THT]
  S10 = Reed switch [package=THT]
  S11 = Reed switch [package=THT]
  S12 = Reed switch [package=THT]
  S14 = Reed switch [package=THT]

nets:
  N1: YwRobot_Power_Supply1.VCC#5, YwRobot_Power_Supply1.VCC#6
  VCC: YwRobot_Power_Supply1.VCC#9, YwRobot_Power_Supply1.VCC#10, Teensy1.Vin, hc-sr1.VCC, hc-sr2.VCC, hc-sr3.VCC, KY-1.signal, KY-2.signal, KY-3.signal, KY-4.signal, S4.leg0
  N2: YwRobot_Power_Supply1.GND#11, YwRobot_Power_Supply1.GND#12
  GND: YwRobot_Power_Supply1.GND#13, YwRobot_Power_Supply1.GND#14, Teensy1.GND, Teensy1.GND1, LED2.anode, LED3.anode, KY-1.ground, KY-2.ground, KY-3.ground, LED4.anode, LED5.anode, Q1.source, Q2.source, Q3.source, R6.Pin_1, R7.Pin_1, R8.Pin_1, LED6.common_cathode, U1.GND, KY-4.ground, R11.Pin_0, R12.Pin_0, R13.Pin_0, LED9.anode, LED11.anode, LED14.anode, LED18.anode, LED22.anode, LED26.anode, LED30.anode, LED34.anode, LED38.anode
  N3: Teensy1.D0, U1.MOSI
  N4: Teensy1.D1, U1.MISO
  N5: Teensy1.D4, U1.NSS
  N6: Teensy1.D7, KY-3.power
  N7: Teensy1.D8, KY-1.power
  N8: Teensy1.D9, KY-2.power
  N9: Teensy1.D10, KY-4.power
  N10: Teensy1.A0/D14, U1.SCK
  N11: Teensy1.A3/D17, S14.pin_1
  N12: Teensy1.A4/D18, hc-sr3.Echo
  N13: Teensy1.A5/D19, hc-sr3.Trig
  N14: Teensy1.A6/D20, hc-sr2.Echo
  N15: Teensy1.A7/D21, hc-sr2.Trig
  N16: Teensy1.A8/D22, hc-sr1.Echo
  N17: Teensy1.A9/D23, hc-sr1.Trig
  3V3: Teensy1.3V3, Teensy1.3V3_1, U1.VCC
  N18: Teensy1.D24, Keypad4x1.Pin1
  N19: Teensy1.D25, Keypad4x1.Pin2
  N20: Teensy1.D26, Keypad4x1.Pin3
  N21: Teensy1.D27, Keypad4x1.Pin4
  N22: Teensy1.D28, Keypad4x1.Pin5
  N23: Teensy1.D29, Keypad4x1.Pin6
  N24: Teensy1.D30, Keypad4x1.Pin7
  N25: Teensy1.D31, Keypad4x1.Pin8
  N26: Teensy1.D32, R10.pin_0, R11.Pin_1
  N27: Teensy1.D33, R12.Pin_1, R14.pin_0
  N28: Teensy1.D34, R13.Pin_1, R15.pin_0
  N29: Teensy1.D35, Q1.gate
  N30: Teensy1.D36, Q2.gate
  N31: Teensy1.D37, Q3.gate
  N32: Teensy1.D38, U1.RST
  N33: hc-sr1.GND, R4.Pin_0
  N34: hc-sr2.GND, R2.Pin_0
  N35: hc-sr3.GND, R3.Pin_0
  N36: LED2.cathode, R3.Pin_1
  N37: LED3.cathode, R2.Pin_1
  N38: S1.pin_1, S9.pin_2
  N39: S1.pin_2, S3.pin_1
  N40: S2.pin_1, S3.pin_2
  N41: S2.pin_2, R5.Pin_0
  N42: KY-1.C, LED7.A
  N43: KY-2.NC, ML1.+
  N44: KY-3.NC, ML2.+
  N45: LED4.cathode, R4.Pin_1
  N46: Q1.drain, R6.Pin_0, LED6.red_anode
  N47: Q2.drain, R7.Pin_0, LED6.green_anode
  N48: Q3.drain, R8.Pin_0, LED6.blue_anode
  N49: KY-4.NC, ML3.+
  N50: S4.leg1, S5.leg0
  N51: S5.leg1, S6.leg0
  N52: S6.leg1, S7.leg0
  N53: S7.leg1, S8.leg0
  N54: S8.leg1, R16.Pin_0, R18.Pin_0, R19.Pin_0, R20.Pin_0, R21.Pin_0, R22.Pin_0, R23.Pin_0, R24.Pin_0
  N55: R10.pin_1, R14.pin_1
  N56: LED9.cathode, R16.Pin_1
  N57: LED11.cathode, R18.Pin_1
  N58: LED14.cathode, R19.Pin_1
  N59: LED18.cathode, R20.Pin_1
  N60: LED22.cathode, R21.Pin_1
  N61: LED26.cathode, R22.Pin_1
  N62: LED30.cathode, R23.Pin_1
  N63: LED34.cathode, R24.Pin_1
  N64: LED38.cathode, R25.Pin_1
  N65: S9.pin_1, S10.pin_2
  N66: S10.pin_1, S11.pin_2
  N67: S11.pin_1, S12.pin_2
  N68: S12.pin_1, S14.pin_2

notes:
  12V source +
  -
  Aici va fi conectat un sirag de leduri RGB SMD5050.Am conecatat doar un led . Am desenat si definit un sirag de leduri insa nu pot defini pinii.
  Electromagnet, desenat si definit de mine. Desenat in aplicatia INKSCAPE si modificat in FRITZING
  Senzori ultrasonici, activati simultan declanseaza un electromagnet ce va deschide un sertar
  220V 50Hz
  Tensiunea de la priza, folosita pentru luminile din camera
  Puzzle nou: Reed
  Se va folosi in combinatie cu matricea de leduri si vor declansa un electromagnet
  Intrerupatoare Reed. Activate simultan, declanseaza un electromagnet. Suporta pana la 24v deci pot fi legate direct la electromagnet(12v)
  Legenda: Firele rosii sunt alimentarea
  Firele negre sunt masa
  Restul de fire sunt de date
  Tatatura(8 pini) si lcd(cu driver=2pini) nu au fost conectate deoarece in aplicatie nu am acces la pinii de pe spatele placutei
  Aici se pune modulul i2c si se conecteaza la pinii A10 si A11 de pe spate controller
  Puzzle nou: Fotocelule
  photocell,detecteaza nivelul de lumina.Rezistenta scade cand lumina se intensifica. Cand sunt acoperite ele se declanseaza
  Puzzle nou:SISTEM SOLAR
  Dedesubt se afla o matrice de leduri.Matricea este dispusa circular, in 8 cercuri, fiecare are 4 leduri dintre care doar unul se va aprinde.MATRICEA IMITA SISTEMUL SOLAR. Apasarea simultana a butoanelor de mai sus vor aprinde doar ledurile conectate. In locul butoanelor simple se pot pune butoane switch cu 2 sau 3 pozitii. Ledurile aprinse indica pozitii ale planetelor. Planetele(sfere ce vor fi gasite de-a lungul jocului) vor fi plasate pe o masa unde se afla desenat sistemul solar, conform ledurilor aprinse. Fiecare planeta va avea inserat un magnet iar in apropierea intrerupatorului Reed ele vor declansa un electromagnet.
  Modul RFID. Detecteaza un tag si sctiveaza jocul de lumini RGB

custom parts:
  YwRobot Breadboard Power Supply: The YwRobot Breadboard Power Supply (MB-V2) has two power rails; they can be 5V or 3V3. Power to the module can be provided through the female USB socket or through the A10 (female) 2.1mm power jack.
  Teensy 3.6 (Basic): The Teensy is a complete USB-based microcontoller development system, in a very small footprint, capable of implementing many types of projects. All programming is done via the USB port. No special programmer is needed, only a standard micro-USB cable and a PC or Macintosh with a USB port.
  Keyes Relay: The Keyes 5V relay module is suitable for SCM development, home appliance control. It uses a 5V~12V TIL control signal which can control DC / AC signal.
  RFID RC522 SIP - 8 pins: A SIP stand-in part for RFID RC522 . With 8 pins on a 300 mil single inline package (SIP) footprint.
  Keypad Membran 4x4: Membrane Keypad 4x4 Matrix
  MagLock: Magnetic Lock.
  LEDs: LEDs Standard schematic elements and footprints for 5mm, 3mm, 1206, and 0603 sized LEDs. 5mm - Spark Fun Electronics SKU : COM-00529 (and others)
  SMD5050 s: A piece of a smd5050 rgb led string. Can be used with Mosfets, IRLZ44N or IRLZ44P and be controlled by a microcontroller
